// Logisim project control.circ as structural Verilog: 1 circuit, main circuit main
module main (
  input  [5:0] instruction_31_26,
  output RegDst,
  output Jump,
  output Branch,
  output MemRead,
  output MemtoReg,
  output [3:0] ALUOp,
  output MemWrite,
  output ALUSrc,
  output RegWrite
);

  wire comparator_2_eq, comparator_3_eq, comparator_6_eq, comparator_7_eq, comparator_8_eq, IsAdd, IsAddU,
       isAnd, isJ, isJAL, isOr, isSLT, isSLTU, xor_1_out;

  Comparator #(.width(6)) comparator_1 (.a(instruction_31_26), .b({6{1'b0}}), .eq(RegDst));  // open: gt, lt
  Comparator #(.width(6)) comparator_2 (.a(instruction_31_26), .b(6'b001000), .eq(comparator_2_eq));  // open: gt, lt
  Comparator #(.width(6)) comparator_3 (.a(instruction_31_26), .b(6'b001111), .eq(comparator_3_eq));  // open: gt, lt
  Comparator #(.width(6)) comparator_4 (.a(instruction_31_26), .b(6'b100011), .eq(MemtoReg));  // open: gt, lt
  Comparator #(.width(6)) comparator_5 (.a(instruction_31_26), .b(6'b101011), .eq(MemWrite));  // open: gt, lt
  Comparator #(.width(6)) comparator_6 (.a(instruction_31_26), .b(6'b000100), .eq(comparator_6_eq));  // open: gt, lt
  or or_1 (Branch, comparator_6_eq, comparator_7_eq, comparator_8_eq);
  Comparator #(.width(6)) comparator_7 (.a(instruction_31_26), .b(6'b000101), .eq(comparator_7_eq));  // open: gt, lt
  Comparator #(.width(6)) comparator_8 (.a(instruction_31_26), .b(6'b000001), .eq(comparator_8_eq));  // open: gt, lt
  Comparator #(.width(6)) comparator_9 (.a(instruction_31_26), .b(6'b001001), .eq(IsAddU));  // open: gt, lt
  Comparator #(.width(6)) comparator_10 (.a(instruction_31_26), .b(6'b001100), .eq(isAnd));  // open: gt, lt
  Comparator #(.width(6)) comparator_11 (.a(instruction_31_26), .b(6'b001101), .eq(isOr));  // open: gt, lt
  Comparator #(.width(6)) comparator_12 (.a(instruction_31_26), .b(6'b001010), .eq(isSLT));  // open: gt, lt
  Comparator #(.width(6)) comparator_13 (.a(instruction_31_26), .b(6'b001011), .eq(isSLTU));  // open: gt, lt
  Comparator #(.width(6)) comparator_14 (.a(instruction_31_26), .b(6'b000011), .eq(isJAL));  // open: gt, lt
  Comparator #(.width(6)) comparator_15 (.a(instruction_31_26), .b(6'b000010), .eq(isJ));  // open: gt, lt
  or or_2 (MemRead, MemtoReg, comparator_3_eq);
  or or_3 (IsAdd, comparator_2_eq, comparator_3_eq, MemtoReg, MemWrite);
  or or_4 (Jump, isJ, isJAL);
  or Op0 (ALUOp[0], isSLTU, isAnd, IsAdd, Branch);
  nor Op1 (ALUOp[1], RegDst, IsAdd, isAnd);
  nor Op1_2 (ALUOp[2], RegDst, isOr, isAnd);
  or Op3 (ALUOp[3], isAnd, isOr, isSLT, isSLTU);
  xor xor_1 (xor_1_out, IsAdd, MemWrite);
  nor nor_1 (ALUSrc, Branch, RegDst);
  or or_5 (RegWrite, RegDst, IsAddU, isSLT, isSLTU, isAnd, isOr, xor_1_out);

  // Other names for the same wires on the sheet: Input[5:0] = instruction_31_26; IsALUSrc = ALUSrc; IsJump = Jump;
  //   IsLoad = MemRead; IsMemRead = MemRead; IsLW = MemtoReg; IsMemToReg = MemtoReg; IsR = RegDst; IsRegDest = RegDst;
  //   IsRegWrite = RegWrite; IsBranch = Branch; IsSub = Branch; IsSW_MemWrite = MemWrite; TheOp[3:0] = ALUOp

  // Notes on the sheet:
  //   Determine Instruction Type
  //   ALUOp
  //   Biggest Concern right now - right now, lui outputs an ALUOp of "add" when in reality it might need to be sll (which hasn't been given a code)
  //   Possible Solution - assign sll to to ALUOp 0001 (which is unused as of now), and fix all of the components that load instructions affect 
endmodule
