// Logisim project cpu.circ as structural Verilog: 1 circuit, main circuit main
module main (
  input  [31:0] INSTRUCTION,
  input  CLOCK,
  output [31:0] FETCH_ADDRESS,
  output [31:0] s0_Value,
  output [31:0] s1_Value,
  output [31:0] s2_Value,
  output [31:0] ra_Value,
  output [31:0] sp_Value,
  output [3:0] swinc
);

  wire and_1_out, Control_alusrc, Control_branch, Control_jal, Control_jump, Control_memtoreg,
       Control_memwrite, Control_regwrite, main_2_equal;
  wire [1:0] Control_regdst;
  wire [3:0] ALU_Control_aluswitch;
  wire [4:0] multiplexer_1_out;
  wire [31:0] adder_2_out, bit_extender_1_out, main_1_read_data_1, main_1_read_data_2, main_2_result,
       main_3_p5, multiplexer_2_out, multiplexer_3_out, multiplexer_4_out, multiplexer_5_out,
       multiplexer_6_out, PC_4, PC_q, shifter_1_out;

  Register #(.width(32)) PC (.D(multiplexer_5_out), .Q(PC_q), .clk(CLOCK));  // open: en, clr
  Adder #(.width(32)) adder_1 (.a(PC_q), .b(32'h4), .out(PC_4));  // open: cin, cout
  Multiplexer #(.select(2), .width(5), .enable("false")) multiplexer_1 (
    .in0(INSTRUCTION[20:16]), .in1(INSTRUCTION[15:11]), .in2({5{1'b1}}), .out(multiplexer_1_out),
    .sel(Control_regdst));  // open: in3
  control_main Control (
    .instruction_31_26(INSTRUCTION[31:26]), .RegDst(Control_regdst), .Jump(Control_jump),
    .Branch(Control_branch), .MemtoReg(Control_memtoreg), .ALUOp(swinc), .MemWrite(Control_memwrite),
    .ALUSrc(Control_alusrc), .RegWrite(Control_regwrite), .JAL(Control_jal));  // open: MemRead
  assign bit_extender_1_out = {{16{INSTRUCTION[15]}}, INSTRUCTION[15:0]};  // Bit_Extender bit_extender_1
  regfile_main main_1 (
    .Read_Register_1(INSTRUCTION[25:21]), .Read_Register_2(INSTRUCTION[20:16]),
    .Write_Register(multiplexer_1_out), .Write_Data(multiplexer_2_out), .Write_Enable(Control_regwrite),
    .Clock(CLOCK), .Read_Data_1(main_1_read_data_1), .Read_Data_2(main_1_read_data_2));  // open: s0_Value, s1_Value, s2_Value, ra_Value, sp_Value
  Multiplexer #(.width(32), .enable("false")) multiplexer_2 (
    .in0(multiplexer_6_out), .in1(PC_4), .out(multiplexer_2_out), .sel(Control_jal));
  Shifter #(.width(32)) shifter_1 (.in(bit_extender_1_out), .\dist (5'b00010), .out(shifter_1_out));
  Multiplexer #(.width(32), .enable("false")) multiplexer_3 (
    .in0(main_1_read_data_2), .in1(bit_extender_1_out), .out(multiplexer_3_out), .sel(Control_alusrc));
  alu_control_main ALU_Control (.Instruction_5_0(INSTRUCTION[5:0]), .ALUOp(swinc), .ALUSwitch(ALU_Control_aluswitch));
  Adder #(.width(32)) adder_2 (.a(PC_4), .b(shifter_1_out), .out(adder_2_out));  // open: cin, cout
  alu_main main_2 (
    .Switch(ALU_Control_aluswitch), .X(main_1_read_data_1), .Equal(main_2_equal), .Result(main_2_result),
    .Y(multiplexer_3_out));  // open: Signed_Overflow
  Multiplexer #(.width(32), .enable("false")) multiplexer_4 (
    .in0(PC_4), .in1(adder_2_out), .out(multiplexer_4_out), .sel(Control_jump));
  and and_1 (and_1_out, Control_branch, main_2_equal);
  Multiplexer #(.width(32), .enable("false")) multiplexer_5 (
    .in0({PC_4[31:28], INSTRUCTION[25:0], 2'b00}), .in1(multiplexer_4_out), .out(multiplexer_5_out),
    .sel(and_1_out));
  // mem_main main_3: pin names not known; wires that end beside it: main_2_result, main_1_read_data_2, Control_memwrite, CLOCK, main_3_p5
  Multiplexer #(.width(32), .enable("false")) multiplexer_6 (
    .in0(main_3_p5), .in1(main_2_result), .out(multiplexer_6_out), .sel(Control_memtoreg));

  // Other names for the same wires on the sheet: clk = CLOCK; fetch_addr[31:0] = FETCH_ADDRESS; ra[31:0] = ra_Value;
  //   s0[31:0] = s0_Value; s1[31:0] = s1_Value; s2[31:0] = s2_Value; sp[31:0] = sp_Value

  // Notes on the sheet:
  //   Output
  //   For JAL, $ra
  //   These are outputs/inputs from run.circ
  //   Inputs
  //   These are DEBUG/TEST outputs from your circuit.
endmodule
